# Fritzing sketch BeerBuddy (saved by Fritzing 0.9.6b)
circuit board: 7.92946cm x 6.13326cm
breadboards: 1

parts:
  Cooling_Pump = DC Motor
  Transistor = pnp-Powertransistor [package="TO220 [THT]"]
  D-1N4148 = Diode [package=sma-diode]
  Pico = Raspberry Pi Pico
  Heat_Power = Power plug
  Transistor1 = pnp-Powertransistor [package="TO220 [THT]"]
  D-1N4149 = Diode [package=sma-diode]
  Heating_Pad = DC Motor
  Thermometer = DS18B20 1-Wire Temperature Sensor [part_number=DS18B20]

nets:
  N1: Cooling_Pump.pin_1, Transistor.collector, D-1N4148.A
  N2: Cooling_Pump.pin_2, D-1N4148.C, Pico.pin_40
  N3: Transistor.base, Pico.pin_29
  GND: Transistor.emitter, Pico.pin_3, Pico.pin_23, Pico.pin_33, Pico.pin_42, Heat_Power.GND, Transistor1.emitter, Thermometer.GND
  N4: Pico.pin_14, Thermometer.DQ
  N5: Pico.pin_27, Transistor1.base
  N6: Pico.pin_37, Thermometer.VDD
  N7: Heat_Power.VCC, D-1N4149.C, Heating_Pad.pin_2
  N8: Transistor1.collector, D-1N4149.A, Heating_Pad.pin_1

custom parts:
  Raspberry Pi Pico: Raspberry Pi Pico. Based around the RP2040 microcontroller the Pico is a low cost microcontroller device bringing Raspberry Pi quality, cost, and easy of use to the microcontroller space. Jan 2021, Split part in to two versions: SMD (this one) and tht. This one is single sided and uses the castellation pads to solder the module to the board (no holes, other than for the USB connector!). The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
